// Logisim project Practica05.circ as structural Verilog
module automata (
  input  In
);

  wire clock_1_out, E1_qn, E2_qn, not_1_out, R1_out, S1_out, S2_out;
  wire [1:0] E2_q;

  Clock clock_1 (.out(clock_1_out));
  not not_1 (not_1_out, In);
  S_R_Flip_Flop E1 (.S(S1_out), .clk(clock_1_out), .R(R1_out), .Q(E2_q[1]), .Qn(E1_qn));  // open: preset, reset, en
  S_R_Flip_Flop E2 (.S(S2_out), .clk(clock_1_out), .R(E2_q[0]), .Q(E2_q[0]), .Qn(E2_qn));  // open: preset, reset, en
  and S1 (S1_out, E1_qn, E2_q[0], not_1_out);
  and R1 (R1_out, E2_q[1], E2_q[0], not_1_out);
  and S2 (S2_out, E2_qn, not_1_out);
  Hex_Digit_Display hex_digit_display_1 (.value({2'b00, E2_q}));  // open: dp

  // Notes on the sheet:
  //   Entrada del autómata
  //   0 = error
  //   1 = acierto
  //   Autómata del ejercicio 1
  //   R2
  //   Estado actual del autómata.
  //   0 = T
  //   1 = TE
  //   2 = NT
  //   3 = NTE
endmodule
